// Logisim project simple_16bit_cpu.circ as structural Verilog: 6 circuits, main circuit CPU
module CPU (
  input  reset,
  output [15:0] out_2,
  output [15:0] out_3,
  output [15:0] out_4,
  output [15:0] out_5
);

  wire alu_1_blecond, alu_1_bnecond, clock_1_out, cu_1_halt, cu_1_memread, cu_1_memwrite, cu_1_pcsrc_branch,
       cu_1_rawrite, cu_1_regwrite, pla_1_out, pla_2_out, pla_3_out;
  wire [1:0] cu_1_aluop, cu_1_branchcond, cu_1_jump, cu_1_regwritesource;
  wire [2:0] op_decode_1_rd, op_decode_1_rs, op_decode_1_rt;
  wire [3:0] op_decode_1_opcode;
  wire [15:0] adder_2_out, multiplexer_1_out, multiplexer_2_out, multiplexer_3_out, op_decode_1_imm,
       pc_1_addr, ram_1_dout, reg_file_1_radata, reg_file_1_wdata1, reg_file_1_wdata2;

  Clock clock_1 (.out(clock_1_out));
  PC pc_1 (
    .jump_address(multiplexer_1_out), .BleCond(alu_1_blecond), .BneCond(alu_1_bnecond),
    .PCSrc_Branch(cu_1_pcsrc_branch), .RaData(reg_file_1_radata), .JumpType(cu_1_jump), .clock(clock_1_out),
    .Halt(cu_1_halt), .reset(reset), .addr(pc_1_addr));
  // Probe on multiplexer_1_out
  ROM #(.addrWidth(16), .dataWidth(16)) rom_1 (.addr(pc_1_addr), .data(out_2));
  Adder #(.width(16)) adder_1 (.a(pc_1_addr), .b(out_4), .out(out_3));  // open: cin, cout
  Multiplexer #(.width(16)) multiplexer_1 (.in0(out_3), .in1(out_4), .out(multiplexer_1_out), .sel(pla_1_out));
  PLA #(.in_width(4), .out_width(1), .\table ("1100 1\n0000 0\n0001 0\n0010 0\n0011 0\n0100 0\n0101 0\n0110 0\n0111 0\n1000 0\n1001 0\n1010 0\n1011 0\n1101 0\n1110 0\n1011 0")) pla_1 (
    .in(op_decode_1_opcode), .out(pla_1_out));
  op_decode op_decode_1 (
    .instruction(out_2), .opcode(op_decode_1_opcode), .rs(op_decode_1_rs), .rt(op_decode_1_rt),
    .rd(op_decode_1_rd), .imm(op_decode_1_imm), .target(out_4));
  Adder #(.width(16)) adder_2 (.a({16{1'b0}}), .b(pc_1_addr), .out(adder_2_out));  // open: cin, cout
  PLA #(.in_width(4), .out_width(1), .\table ("0100 0\n0101 0\n0110 0\n0000 1\n0001 1\n0010 1\n0011 1\n0111 1\n1010 0\n1011 0\n1001 1")) pla_2 (
    .in(op_decode_1_opcode), .out(pla_2_out));
  CU cu_1 (
    .opcode(op_decode_1_opcode), .RegWrite(cu_1_regwrite), .ALUOp(cu_1_aluop), .MemRead(cu_1_memread),
    .MemWrite(cu_1_memwrite), .PCSrc_Branch(cu_1_pcsrc_branch), .BranchCond(cu_1_branchcond),
    .RaWrite(cu_1_rawrite), .Halt(cu_1_halt), .RegWriteSource(cu_1_regwritesource), .Jump(cu_1_jump));
  REG_file reg_file_1 (
    .write(cu_1_regwrite), .writeregister(op_decode_1_rd), .ALUresult(out_5), .load(ram_1_dout),
    .read1(op_decode_1_rs), .read2(op_decode_1_rt), .clock(clock_1_out), .reset(reset), .li(op_decode_1_imm),
    .RegWriteSource(cu_1_regwritesource), .PC(adder_2_out), .raWrite(cu_1_rawrite),
    .wdata1(reg_file_1_wdata1), .wdata2(reg_file_1_wdata2), .RaData(reg_file_1_radata));
  // Probe on reg_file_1_wdata2
  Multiplexer #(.width(16)) multiplexer_2 (
    .in0(reg_file_1_wdata1), .in1(reg_file_1_wdata2), .out(multiplexer_2_out), .sel(pla_3_out));
  Multiplexer #(.width(16)) multiplexer_3 (
    .in0(reg_file_1_wdata2), .in1(op_decode_1_imm), .out(multiplexer_3_out), .sel(pla_2_out));
  // Probe on op_decode_1_imm
  // Probe on multiplexer_3_out
  PLA #(.in_width(4), .out_width(1), .\table ("0100 0\n0101 0\n0110 0\n0000 1\n0001 1\n0010 1\n0011 1\n0111 0\n1010 0\n1011 0\n1001 1")) pla_3 (
    .in(op_decode_1_opcode), .out(pla_3_out));
  // Probe on out_5
  RAM #(.addrWidth(16), .dataWidth(16)) ram_1 (
    .addr(out_5), .we(cu_1_memwrite), .oe(cu_1_memread), .clk(clock_1_out), .din(reg_file_1_wdata1),
    .dout(ram_1_dout));
  // Probe on reg_file_1_wdata1
  ALU alu_1 (
    .RegData1(multiplexer_2_out), .RegData2(multiplexer_3_out), .ALUOp(cu_1_aluop),
    .BranchCond(cu_1_branchcond), .ALUResult(out_5), .BleCond(alu_1_blecond), .BneCond(alu_1_bnecond));

  // Notes on the sheet:
  //   contents of rom_1 (hex, n*v repeats v):
  //   6 204 d007 7680 7 208 d003 7880 c003 4014 e000 f000
endmodule

module REG_file (
  input  write,
  input  [2:0] writeregister,
  input  [15:0] ALUresult,
  input  [15:0] load,
  input  [2:0] read1,
  input  [2:0] read2,
  input  clock,
  input  reset,
  input  [15:0] li,
  input  [1:0] RegWriteSource,
  input  [15:0] PC,
  input  raWrite,
  output [15:0] wdata1,
  output [15:0] wdata2,
  output [15:0] RaData
);

  wire and_1_out, and_2_out, and_3_out, and_4_out, and_5_out, and_6_out, and_7_out, and_8_out,
       decoder_1_out0, decoder_1_out1, decoder_1_out2, decoder_1_out3, decoder_1_out4, decoder_1_out5,
       decoder_1_out6, decoder_1_out7;
  wire [15:0] adder_1_out, multiplexer_1_out, register_2_q, register_3_q, register_4_q, register_5_q,
       register_6_q, register_7_q, register_8_q, register_9_q;

  Decoder #(.enable("false"), .select(3)) decoder_1 (
    .out0(decoder_1_out0), .out1(decoder_1_out1), .out2(decoder_1_out2), .out3(decoder_1_out3),
    .out4(decoder_1_out4), .out5(decoder_1_out5), .out6(decoder_1_out6), .out7(decoder_1_out7),
    .sel(writeregister));
  Multiplexer #(.select(2), .width(16)) multiplexer_1 (
    .in0(ALUresult), .in1(load), .in2(li), .in3({16{1'b0}}), .out(multiplexer_1_out), .sel(RegWriteSource));
  and and_1 (and_1_out, decoder_1_out0, write);
  and and_2 (and_2_out, decoder_1_out1, write);
  and and_3 (and_3_out, decoder_1_out2, write);
  and and_4 (and_4_out, decoder_1_out3, write);
  and and_5 (and_5_out, decoder_1_out4, write);
  and and_6 (and_6_out, decoder_1_out5, write);
  and and_7 (and_7_out, decoder_1_out6, write);
  and and_8 (and_8_out, decoder_1_out7, write);
  Adder #(.width(16)) adder_1 (.a(PC), .b(16'h1), .out(adder_1_out));  // open: cin, cout
  Register #(.width(16)) register_1 (.D(adder_1_out), .en(raWrite), .clk(clock), .Q(RaData), .clr(reset));
  Register #(.width(16)) register_2 (.D(multiplexer_1_out), .en(and_1_out), .clk(clock), .Q(register_2_q), .clr(reset));
  Register #(.width(16)) register_3 (.D(multiplexer_1_out), .en(and_2_out), .clk(clock), .Q(register_3_q), .clr(reset));
  Register #(.width(16)) register_4 (.D(multiplexer_1_out), .en(and_3_out), .clk(clock), .Q(register_4_q), .clr(reset));
  Register #(.width(16)) register_5 (.D(multiplexer_1_out), .en(and_4_out), .clk(clock), .Q(register_5_q), .clr(reset));
  Register #(.width(16)) register_6 (.D(multiplexer_1_out), .en(and_5_out), .clk(clock), .Q(register_6_q), .clr(reset));
  Register #(.width(16)) register_7 (.D(multiplexer_1_out), .en(and_6_out), .clk(clock), .Q(register_7_q), .clr(reset));
  Register #(.width(16)) register_8 (.D(multiplexer_1_out), .en(and_7_out), .clk(clock), .Q(register_8_q), .clr(reset));
  Register #(.width(16)) register_9 (.D(multiplexer_1_out), .en(and_8_out), .clk(clock), .Q(register_9_q), .clr(reset));
  Multiplexer #(.select(3), .width(16)) multiplexer_2 (
    .in0(register_2_q), .in1(register_3_q), .in2(register_4_q), .in3(register_5_q), .in4(register_6_q),
    .in5(register_7_q), .in6(register_8_q), .in7(register_9_q), .out(wdata1), .sel(read1));
  Multiplexer #(.select(3), .width(16)) multiplexer_3 (
    .in0(register_2_q), .in1(register_3_q), .in2(register_4_q), .in3(register_5_q), .in4(register_6_q),
    .in5(register_7_q), .in6(register_8_q), .in7(register_9_q), .out(wdata2), .sel(read2));
endmodule

module ALU (
  input  [15:0] RegData1,
  input  [15:0] RegData2,
  input  [1:0] ALUOp,
  input  [1:0] BranchCond,
  output [15:0] ALUResult,
  output BleCond,
  output BneCond
);

  wire comparator_1_eq, comparator_1_gt, not_1_out, not_2_out;
  wire [15:0] adder_1_out, and_1_out, or_1_out;

  Comparator #(.width(16)) comparator_1 (
    .a(RegData1), .b(RegData2), .gt(comparator_1_gt), .eq(comparator_1_eq));  // open: lt
  Adder #(.width(16)) adder_1 (.a(RegData1), .b(RegData2), .out(adder_1_out));  // open: cin, cout
  not not_1 (not_1_out, comparator_1_gt);
  not not_2 (not_2_out, comparator_1_eq);
  assign and_1_out = RegData1 & RegData2;  // AND_Gate and_1, 16 bits wide
  assign or_1_out = RegData1 | RegData2;  // OR_Gate or_1, 16 bits wide
  Multiplexer #(.select(2), .width(16)) multiplexer_1 (
    .in0(adder_1_out), .in1(and_1_out), .in2(or_1_out), .in3(RegData2), .out(ALUResult), .sel(ALUOp));
  and and_2 (BleCond, BranchCond[0], not_1_out);
  and and_3 (BneCond, not_2_out, BranchCond[1]);
endmodule

module PC (
  input  [15:0] jump_address,
  input  BleCond,
  input  BneCond,
  input  PCSrc_Branch,
  input  [15:0] RaData,
  input  [1:0] JumpType,
  input  clock,
  input  Halt,
  input  reset,
  output [15:0] addr
);

  wire not_1_out;
  wire [1:0] and_1_out, and_2_out, bit_extender_1_out, bit_extender_2_out, bit_extender_3_out,
       multiplexer_2_out, or_1_out, or_2_out;
  wire [15:0] adder_1_out, multiplexer_1_out, multiplexer_3_out, multiplexer_4_out;

  assign bit_extender_1_out = {{1{BleCond}}, BleCond};  // Bit_Extender bit_extender_1
  assign bit_extender_2_out = {{1{BneCond}}, BneCond};  // Bit_Extender bit_extender_2
  assign bit_extender_3_out = {{1{PCSrc_Branch}}, PCSrc_Branch};  // Bit_Extender bit_extender_3
  assign or_1_out = bit_extender_1_out | JumpType | bit_extender_2_out;  // OR_Gate or_1, 2 bits wide
  assign and_1_out = or_1_out & bit_extender_3_out;  // AND_Gate and_1, 2 bits wide
  assign and_2_out = bit_extender_3_out & JumpType;  // AND_Gate and_2, 2 bits wide
  assign or_2_out = and_1_out | and_2_out;  // OR_Gate or_2, 2 bits wide
  not not_1 (not_1_out, Halt);
  // Probe on multiplexer_4_out
  Multiplexer #(.select(2), .width(16)) multiplexer_1 (
    .in1(jump_address), .out(multiplexer_1_out), .sel(or_1_out));  // open: in0, in2, in3
  Multiplexer #(.select(2), .width(2)) multiplexer_2 (
    .in0(JumpType), .in1(2'b00), .in2(2'b01), .in3(2'b00), .out(multiplexer_2_out), .sel(JumpType));
  // Probe on multiplexer_2_out
  Register #(.width(16)) register_1 (.D(multiplexer_4_out), .en(not_1_out), .Q(addr), .clk(clock), .clr(reset));
  Adder #(.width(16)) adder_1 (.a(addr), .b(16'h1), .out(adder_1_out));  // open: cin, cout
  Multiplexer #(.select(2), .width(16)) multiplexer_3 (
    .in0(adder_1_out), .in1(multiplexer_1_out), .out(multiplexer_3_out), .sel(or_2_out));  // open: in2, in3
  Multiplexer #(.select(2), .width(16)) multiplexer_4 (
    .in0(multiplexer_3_out), .in1(RaData), .out(multiplexer_4_out), .sel(multiplexer_2_out));  // open: in2, in3
  // Probe on multiplexer_4_out
endmodule

module op_decode (
  input  [15:0] instruction,
  output [3:0] opcode,
  output [2:0] rs,
  output [2:0] rt,
  output [2:0] rd,
  output [15:0] imm,
  output [15:0] target
);

  wire [1:0] pla_1_out;
  wire [2:0] multiplexer_1_out;
  wire [15:0] bit_extender_1_out, bit_extender_2_out;

  PLA #(.in_width(4), .\table ("0100 00\n0101 00\n0110 00\n0111 01\n0000 01\n0001 01\n0010 01\n0011 01\n1000 01\n1001 01\n1010 10\n1011 10\n1100 11\n1101 11")) pla_1 (
    .in(instruction[15:12]), .out(pla_1_out));
  assign bit_extender_1_out = {{10{instruction[5]}}, instruction[5:0]};  // Bit_Extender bit_extender_1
  assign bit_extender_2_out = {{4{instruction[11]}}, instruction[11:0]};  // Bit_Extender bit_extender_2
  // Probe on bit_extender_1_out
  // Probe on instruction[8:6]
  // Probe on instruction[11:9]
  // Probe on instruction[8:6]
  // Probe on pla_1_out
  Multiplexer #(.select(2), .width(3)) multiplexer_1 (
    .in0(instruction[8:6]), .in1(instruction[11:9]), .out(multiplexer_1_out), .sel(pla_1_out));  // open: in2, in3
  // Probe on multiplexer_1_out
  Multiplexer #(.select(2), .width(3)) multiplexer_2 (
    .in0(instruction[9:7]), .in1(instruction[8:6]), .in2(instruction[11:9]), .out(rs), .sel(pla_1_out));  // open: in3
  Multiplexer #(.select(2), .width(3)) multiplexer_3 (
    .in0(instruction[6:4]), .in1(instruction[11:9]), .in2(instruction[8:6]), .out(rt), .sel(pla_1_out));  // open: in3
  Multiplexer #(.select(2), .width(3)) multiplexer_4 (
    .in0(instruction[3:1]), .in1(multiplexer_1_out), .out(rd), .sel(pla_1_out));  // open: in2, in3
  Multiplexer #(.select(2), .width(16)) multiplexer_5 (
    .in1(bit_extender_1_out), .out(imm), .sel(pla_1_out));  // open: in0, in2, in3
  Multiplexer #(.select(2), .width(16)) multiplexer_6 (
    .in2(bit_extender_1_out), .in3(bit_extender_2_out), .out(target), .sel(pla_1_out));  // open: in0, in1

  assign opcode = instruction[15:12];
endmodule

module CU (
  input  [3:0] opcode,
  output RegWrite,
  output [1:0] ALUOp,
  output MemRead,
  output MemWrite,
  output PCSrc_Branch,
  output [1:0] BranchCond,
  output RaWrite,
  output Halt,
  output [1:0] RegWriteSource,
  output [1:0] Jump
);

  PLA #(.in_width(4), .out_width(14), .\table ("0000 00000000000111\n0001 00000000000001\n0010 00000000000011\n0011 00000000000101\n0100 00000000000001\n0101 00000000000011\n0110 00000000000101\n0111 00000000000001\n1000 00010000001001\n1001 00000000010000\n1010 00000001100000\n1011 00000010100000\n1100 01000000100000\n1101 01000100100000\n1110 10000000100000\n1111 00001000000000")) pla_1 (
    .in(opcode),
    .out({Jump, RegWriteSource, Halt, RaWrite, BranchCond, PCSrc_Branch, MemWrite, MemRead, ALUOp, RegWrite}));
endmodule
